// Digital circuit CompletePipelinedProcessor.dig as structural Verilog
module CompletePipelinedProcessor (
  input  C,
  output [7:0] Mdata,
  output [3:0] Op,
  output [15:0] RSdata,
  output [15:0] RTdata,
  output [2:0] RT,
  output [2:0] RS,
  output [7:0] regout,
  output [7:0] instr_low,
  output [7:0] read_output,
  output [15:0] ProgramOutput,
  output [7:0] WriteData
);

  wire ALUSrc, and_1_out, and_2_out, b, Branch, c_2, exemem_1_p8, firstbit, Jump, load_store, load_storein,
       LoadLow, LoadLowIn, MemR, MemRin, MemW, memwb_1_p3, memwb_1_p4, memwb_1_p5, memwb_1_p8, MemWin,
       multiplexer_10_out, N, not_1_out, not_2_out, Offset, PC_disable, RegDst, RegWin, rom_1_d, rom_2_d,
       Wenable, WenOut, Z;
  wire [2:0] RegWritingToOut, RWrite, RwritingToIn;
  wire [3:0] ALUOp, cpustateseq_1_aluop, Op1, OpForWB;
  wire [5:0] ifid_1_p4;
  wire [7:4] reg8_2_o_2;
  wire [9:0] cpustateseq_1_regdst;
  wire [11:0] ifid_1_p3;
  wire [15:0] adder_1_p3, adder_2_p3, adder_4_p3, alu1_1_y, exemem_1_p9, memwb_1_p6, memwb_1_p7,
       multiplexer_1_out, multiplexer_2_out, multiplexer_3_out, multiplexer_7_out, multiplexer_9_out, r2,
       reg_pc_1_do, RegDataIn, RegDataOut, signextimm_start_1_p2;
  wire [15:8] reg8_2_o;

  Multiplexer #(.Bits(16)) multiplexer_1 (.sel(b), .in_0(adder_1_p3), .in_1(adder_2_p3), .out(multiplexer_1_out));
  Multiplexer #(.Bits(16)) multiplexer_2 (
    .sel(Jump), .in_0(multiplexer_1_out), .in_1({reg8_2_o, instr_low}), .out(multiplexer_2_out));
  Reg_PC reg_pc_1 (.Di(multiplexer_2_out), .C(C), .Do(reg_pc_1_do));
  // Chalf chalf_1: pin names not known; wires that end beside it: C, c_2
  Multiplexer #(.Bits(16)) multiplexer_3 (.sel(PC_disable), .in_0(16'h1), .in_1({16{1'b0}}), .out(multiplexer_3_out));
  // Instr_Memory instr_memory_1: pin names not known; wires that end beside it: reg_pc_1_do, instr_low
  // Adder adder_1: pin names not known; wires that end beside it: reg_pc_1_do, multiplexer_3_out, adder_1_p3
  CPUStateSeq cpustateseq_1 (
    .Op(Op), .C(C), .RegDst(cpustateseq_1_regdst[9]), .Branch(cpustateseq_1_regdst[8]),
    .MemR(cpustateseq_1_regdst[7]), .Mem2Reg(cpustateseq_1_regdst[6]), .ALUOp(cpustateseq_1_aluop),
    .MemW(cpustateseq_1_regdst[5]), .ALUSrc(cpustateseq_1_regdst[4]), .RWrite(cpustateseq_1_regdst[3]),
    .PC_disable(PC_disable), .load_store(cpustateseq_1_regdst[2]), .firstbit(firstbit), .Jump(Jump),
    .Offset(cpustateseq_1_regdst[1]), .LoadLow(cpustateseq_1_regdst[0]));  // open: NextSt
  Reg8 reg8_1 (.e(firstbit), .I(instr_low), .C(C), .O({Op, regout[3:0]}));
  Reg8 reg8_2 (.e(firstbit), .I(instr_low), .C(C), .O({reg8_2_o_2, reg8_2_o[11:8]}));
  // IFID ifid_1: pin names not known; wires that end beside it: adder_1_p3, {regout[3:0], instr_low}, {reg8_2_o[15:12], ifid_1_p3}, {RS, RT, ifid_1_p4}
  Multiplexer #(.Bits(3)) multiplexer_4 (.sel(RegDst), .in_0(RT), .in_1(ifid_1_p4[5:3]), .out(RwritingToIn));
  ROM #(.AddrBits(4)) rom_1 (.A(OpForWB), .sel(1'b1), .D(rom_1_d));
  Multiplexer #(.Bits(20)) multiplexer_5 (
    .sel(rom_1_d), .in_0({RwritingToIn, RegWin, RegDataIn}), .in_1({RWrite, Wenable, ProgramOutput}),
    .out({RegWritingToOut, WenOut, RegDataOut}));
  Multiplexer #(.Bits(16)) multiplexer_6 (.sel(LoadLowIn), .in_0(alu1_1_y), .in_1({{15{1'b0}}, N}), .out(RegDataIn));
  Register_File register_file_1 (
    .Rdata1(RSdata), .Rdata2(RTdata), .Wdata(RegDataOut), .Wen(WenOut), .Rwrite(RegWritingToOut), .C(C),
    .Rreg1(RS), .Rreg2(RT));
  // SignExtImm_Start signextimm_start_1: pin names not known; wires that end beside it: ifid_1_p4, signextimm_start_1_p2
  and and_1 (and_1_out, Branch, Z);
  and and_2 (and_2_out, Branch, ~Z);  // And
  Multiplexer #(.Bits(16)) multiplexer_7 (
    .sel(Offset), .in_0({16{1'b0}}), .in_1(signextimm_start_1_p2), .out(multiplexer_7_out));
  ROM #(.AddrBits(4)) rom_2 (.A(Op1), .sel(1'b1), .D(rom_2_d));
  Multiplexer multiplexer_8 (.sel(rom_2_d), .in_0(and_1_out), .in_1(and_2_out), .out(b));
  // Adder adder_2: pin names not known; wires that end beside it: {reg8_2_o[15:12], ifid_1_p3}, signextimm_start_1_p2, adder_2_p3
  Multiplexer #(.Bits(16)) multiplexer_9 (
    .sel(ALUSrc), .in_0(r2), .in_1(signextimm_start_1_p2), .out(multiplexer_9_out));
  // Adder adder_3: pin names not known; wires that end beside it: RTdata, multiplexer_7_out, r2, RwritingToIn, Op1, C
  Multiplexer multiplexer_10 (.sel(load_storein), .in_0(1'b0), .in_1(1'b1), .out(multiplexer_10_out));
  ALU1 alu1_1 (
    .A(RSdata), .B(multiplexer_9_out), .Op({1'b0, ALUOp}), .Y(alu1_1_y), .Zero(Z), .Neg(N),
    .Ci(multiplexer_10_out));  // open: Carry
  // exemem exemem_1: pin names not known; wires that end beside it: alu1_1_y, RTdata, load_storein, MemWin, MemRin, LoadLowIn, c_2, exemem_1_p8, exemem_1_p9, load_store, MemW, MemR
  Multiplexer #(.Bits(8)) multiplexer_11 (
    .sel(not_1_out), .in_0(exemem_1_p9[7:0]), .in_1(exemem_1_p9[15:8]), .out(WriteData));
  not not_1 (not_1_out, load_store);
  // Adder adder_4: pin names not known; wires that end beside it: exemem_1_p8, {{15{1'b0}}, LoadLow}, adder_4_p3
  Data_Memory data_memory_1 (.Addr(adder_4_p3), .Wdata(WriteData), .C(C), .MemR(MemR), .MemW(MemW), .Rdata(Mdata));
  Reg8 reg8_3 (.e(LoadLow), .I(Mdata), .C(C), .O(read_output));
  // MemWb memwb_1: pin names not known; wires that end beside it: {read_output, Mdata}, adder_4_p3, memwb_1_p3, memwb_1_p4, memwb_1_p5, memwb_1_p6, memwb_1_p7, memwb_1_p8
  Multiplexer #(.Bits(16)) multiplexer_12 (.sel(not_2_out), .in_0(memwb_1_p6), .in_1(memwb_1_p7), .out(ProgramOutput));
  not not_2 (not_2_out, memwb_1_p8);

  assign regout[7:4] = Op;

  // Other names for the same wires on the sheet: sltdata[0] = N; r_original[15:0] = RTdata;
  //   Wdata[15:0] = ProgramOutput

  // Notes on the sheet:
  //   op|rs|rt|imm
  //   op|rs|rt|rd
  //   Writeback Logic
  //   contents of rom_1 (hex, n*v repeats v):
  //   12*0,1
  //   Branch Logic
  //   contents of rom_2 (hex, n*v repeats v):
  //   6*0,1
endmodule
