// Digital circuit CPUStateSeq.dig as structural Verilog
module CPUStateSeq (
  input  [3:0] Op,
  input  C,
  output RegDst,
  output Branch,
  output MemR,
  output Mem2Reg,
  output [3:0] ALUOp,
  output MemW,
  output ALUSrc,
  output RWrite,
  output [1:0] NextSt,
  output PC_disable,
  output load_store,
  output firstbit,
  output Jump,
  output Offset,
  output LoadLow
);

  wire ALUSrc_t, Branch_t, enable, Jump_t, loadlowreal, not_1_out, RegDst_t, simplecontrol_1_mem2reg,
       simplecontrol_1_memr, simplecontrol_1_memw, simplecontrol_1_rwrite, slt, statecontrol_1_mem2reg,
       statecontrol_1_memr, statecontrol_1_memw, statecontrol_1_rwrite;
  wire [1:0] register_1_q, rom_1_d;
  wire [3:0] simplecontrol_1_aluop, statecontrol_1_aluop;

  ROM #(.AddrBits(4), .Bits(2)) rom_1 (.A(Op), .sel(1'b1), .D(rom_1_d));
  Register #(.Bits(2)) register_1 (.D(NextSt), .C(C), .en(1'b1), .Q(register_1_q));
  StateControl statecontrol_1 (
    .Op(rom_1_d), .St(register_1_q), .MemR(statecontrol_1_memr), .Mem2Reg(statecontrol_1_mem2reg),
    .ALUOp(statecontrol_1_aluop), .MemW(statecontrol_1_memw), .RWrite(statecontrol_1_rwrite),
    .NextSt(NextSt), .firstbit(firstbit), .load_store(load_store), .PC_disable(PC_disable), .enable(enable),
    .offset(Offset), .LoadLow(loadlowreal));
  SimpleControl simplecontrol_1 (
    .Op(Op), .enable(enable), .RegDst(RegDst_t), .Branch(Branch_t), .MemR(simplecontrol_1_memr),
    .Mem2Reg(simplecontrol_1_mem2reg), .ALUOp(simplecontrol_1_aluop), .MemW(simplecontrol_1_memw),
    .ALUSrc(ALUSrc_t), .RWrite(simplecontrol_1_rwrite), .Jump(Jump_t), .loadlow(slt));  // open: Offset
  not not_1 (not_1_out, enable);
  Multiplexer multiplexer_1 (.sel(enable), .in_0(1'b0), .in_1(RegDst_t), .out(RegDst));
  Multiplexer multiplexer_2 (.sel(enable), .in_0(statecontrol_1_memr), .in_1(simplecontrol_1_memr), .out(MemR));
  Multiplexer multiplexer_3 (.sel(enable), .in_0(1'b0), .in_1(Jump_t), .out(Jump));
  Multiplexer #(.Bits(4)) multiplexer_4 (
    .sel(not_1_out), .in_0(simplecontrol_1_aluop), .in_1(statecontrol_1_aluop), .out(ALUOp));
  Multiplexer multiplexer_5 (
    .sel(enable), .in_0(statecontrol_1_mem2reg), .in_1(simplecontrol_1_mem2reg), .out(Mem2Reg));
  Multiplexer multiplexer_6 (.sel(enable), .in_0(statecontrol_1_memw), .in_1(simplecontrol_1_memw), .out(MemW));
  Multiplexer multiplexer_7 (.sel(enable), .in_0(statecontrol_1_rwrite), .in_1(simplecontrol_1_rwrite), .out(RWrite));
  Multiplexer multiplexer_8 (.sel(enable), .in_0(1'b0), .in_1(Branch_t), .out(Branch));
  Multiplexer multiplexer_9 (.sel(enable), .in_0(1'b0), .in_1(ALUSrc_t), .out(ALUSrc));
  Multiplexer multiplexer_10 (.sel(enable), .in_0(loadlowreal), .in_1(slt), .out(LoadLow));

  // Notes on the sheet:
  //   contents of rom_1 (hex, n*v repeats v):
  //   12*0,2,1
  //   For codes see PA 4.5.4.
  //   Only the control signals 
  //   used in the single cycle
  //   CPU are included here.  
  //   ALUSrc is the msb
  //   of ALUSrcB
  //   00 = R-type
  //   01 = SW
  //   10 = LW
  //   11 = BEQ
endmodule
