// Digital circuit Data Memory.dig as structural Verilog
module Data_Memory (
  input  [15:0] Addr,
  input  [7:0] Wdata,
  input  C,
  input  MemR,
  input  MemW,
  output [7:0] Rdata
);

  RAMDualPort #(.AddrBits(16), .Bits(8)) ramdualport_1 (.A(Addr), .Din(Wdata), .str(MemW), .C(C), .ld(MemR), .D(Rdata));
endmodule
