// Digital circuit IFID.dig as structural Verilog
module IFID (
  input  e,
  input  [15:0] Pi,
  input  [11:0] Ii,
  input  [17:0] Si,
  input  C,
  output [15:0] Po,
  output [11:0] Io,
  output [17:0] So
);

  Register #(.Bits(46)) register_1 (.D({Pi, Ii, Si}), .C(C), .en(e), .Q({Po, Io, So}));
  // Pins of 14 and 18 bits meet at Si
  // Pins of 13 and 18 bits meet at So
endmodule
