// Digital circuit Instr Memory.dig as structural Verilog
module Instr_Memory (
  input  [15:0] Addr,
  output [15:0] Instr
);

  ROM #(.AddrBits(16), .Bits(8)) rom_1 (.A(Addr), .sel(1'b1), .D(Instr[7:0]));
  // Pins of 8 and 16 bits meet at Instr

  // Notes on the sheet:
  //   contents of rom_1 (hex, n*v repeats v):
  //   52,4b,54,8a,d6,45,d6,80,14,10,c7,5,c6,40,56,c1,93,3c,63,2,90,82
  //   ,90,c1,e0,14,93,1,0,0,12,8,14,10,52,50,d4,4c
endmodule
