// Digital circuit MemWb.dig as structural Verilog
module MemWb (
  input  e,
  input  C,
  input  [15:0] memin,
  input  [15:0] datain,
  input  Mem2RegIn,
  input  WEin,
  input  [2:0] RWriteIn,
  input  [3:0] Op2,
  output [15:0] memout,
  output [15:0] dataout,
  output Mem2Reg,
  output Wenable,
  output [2:0] RWrite,
  output [3:0] Op3
);

  Register #(.Bits(41)) register_1 (
    .D({Op2, RWriteIn, WEin, Mem2RegIn, datain, memin}), .C(C), .en(e),
    .Q({Op3, RWrite, Wenable, Mem2Reg, dataout, memout}));
  // Pins of 3 and 4 bits meet at Op2
endmodule
