// Digital circuit Reg PC.dig as structural Verilog
module Reg_PC (
  input  [15:0] Di,
  input  C,
  output [15:0] Do
);

  Register #(.Bits(16)) register_1 (.D(Di), .C(C), .en(1'b1), .Q(Do));
endmodule
