// Digital circuit Reg8.dig as structural Verilog
module Reg8 (
  input  e,
  input  [7:0] I,
  input  C,
  output [7:0] O
);

  Register #(.Bits(8)) register_1 (.D(I), .C(C), .en(e), .Q(O));
endmodule
