// Digital circuit Register File.dig as structural Verilog
module Register_File (
  input  [2:0] Rreg1,
  input  [2:0] Rreg2,
  input  [15:0] Wdata,
  input  C,
  input  [2:0] Rwrite,
  input  Wen,
  output [15:0] Rdata1,
  output [15:0] Rdata2
);

  RegisterFile #(.AddrBits(3), .Bits(16)) registerfile_1 (
    .Din(Wdata), .we(Wen), .Rw(Rwrite), .C(C), .Ra(Rreg1), .Rb(Rreg2), .Da(Rdata1), .Db(Rdata2));
endmodule
