// Digital circuit SimpleControl.dig as structural Verilog
module SimpleControl (
  input  [3:0] Op,
  input  enable,
  output RegDst,
  output Branch,
  output MemR,
  output Mem2Reg,
  output [3:0] ALUOp,
  output MemW,
  output ALUSrc,
  output RWrite,
  output Jump,
  output Offset,
  output loadlow
);

  ROM #(.AddrBits(4), .isProgramMemory("true"), .Bits(14)) rom_1 (
    .A(Op), .sel(enable),
    .D({loadlow, Offset, Jump, RegDst, Branch, MemR, Mem2Reg, ALUOp, MemW, ALUSrc, RWrite}));

  // Notes on the sheet:
  //   contents of rom_1 (hex, n*v repeats v):
  //   0,19,23,431,40d,b,210,2411,202,610,41,449,118b,108e,800,800
endmodule
