// Digital circuit StateControl.dig as structural Verilog
module StateControl (
  input  [1:0] Op,
  input  [1:0] St,
  output MemR,
  output Mem2Reg,
  output [3:0] ALUOp,
  output MemW,
  output RWrite,
  output [1:0] NextSt,
  output firstbit,
  output load_store,
  output PC_disable,
  output enable,
  output offset,
  output LoadLow
);

  ROM #(.AddrBits(4), .isProgramMemory("true"), .Bits(16)) rom_1 (
    .A({Op, St}), .sel(1'b1),
    .D({LoadLow, offset, enable, firstbit, load_store, PC_disable, Mem2Reg, ALUOp, MemR, MemW, RWrite, NextSt}));

  // Notes on the sheet:
  //   Op|State|Control|NextState
  //   contents of rom_1 (hex, n*v repeats v):
  //   1001,2000,0,0,1001,6a08,6a08,0,1001,6a14,ea14,5*0,401,22,25,404
  //   ,210,40,107,1010,80,7*0,401,22,23,404,210,40,107,1010,80,7*0,401
  //   ,28,22,404,210,40,107,1010,80
  //   Control Signals
endmodule
