// Digital circuit exemem.dig as structural Verilog
module exemem (
  input  e,
  input  C,
  input  [15:0] ALUresult,
  input  [15:0] RegIn,
  input  load_storein,
  input  MemWin,
  input  MemRin,
  input  LoadLowin,
  input  Mem2Regin,
  input  RegWin,
  input  [2:0] RwritingToIn,
  input  [3:0] Op1,
  output [15:0] ResultOut,
  output [15:0] datatomem,
  output load_store,
  output MemW,
  output MemR,
  output Loadlow,
  output Mem2Reg,
  output RegW,
  output [2:0] RWritingTo,
  output [3:0] Op2
);

  Register #(.Bits(45)) register_1 (
    .D({Op1, RwritingToIn, RegWin, Mem2Regin, LoadLowin, MemRin, MemWin, load_storein, RegIn, ALUresult}),
    .C(C), .en(e), .Q({Op2, RWritingTo, RegW, Mem2Reg, Loadlow, MemR, MemW, load_store, datatomem, ResultOut}));
endmodule
